# Fritzing sketch gehoertrainer (saved by Fritzing 0.9.2b)
circuit board: 8.46667cm x 5.64444cm
breadboards: 1

parts:
  LCD2 = LCD screen
  LCM1602_IIC2 = LCM1602 IIC [part_number="LCM1602 IIC" chip_label="LCM1602 IIC" package="DIP (Dual Inline) [THT]"]
  Bauteil1 = Arduino Nano (Rev3.0)
  S1 = Pushbutton [package="[SMD]"]
  S2 = Pushbutton [package="[SMD]"]
  S3 = Pushbutton [package="[SMD]"]
  S4 = Pushbutton [package="[SMD]"]
  J1 = Piezo Speaker
  VCC1 = Battery block 9V
  R1 = Resistor [tolerance=±5% resistance=100 package=THT]
  C1 = Capacitor [package=cap-pth-small2]
  R2 = Resistor [tolerance=±5% resistance=100k package=THT]
  R3 = Resistor [tolerance=±5% resistance=100k package=THT]
  U1 = LM358 [package=dip08]

nets:
  VSS: LCD2.VSS, LCM1602_IIC2.VSS
  VDD: LCD2.VDD, LCM1602_IIC2.VDD
  N1: LCD2.V0, LCM1602_IIC2.V0
  N2: LCD2.RS, LCM1602_IIC2.RS
  N3: LCD2.R/W, LCM1602_IIC2.RW
  N4: LCD2.E, LCM1602_IIC2.E
  N5: LCD2.DB0, LCM1602_IIC2.D0
  N6: LCD2.DB1, LCM1602_IIC2.D1
  N7: LCD2.DB2, LCM1602_IIC2.D2
  N8: LCD2.DB3, LCM1602_IIC2.D3
  N9: LCD2.DB4, LCM1602_IIC2.D4
  N10: LCD2.DB5, LCM1602_IIC2.D5
  N11: LCD2.DB6, LCM1602_IIC2.D6
  N12: LCD2.DB7, LCM1602_IIC2.D7
  N13: LCD2.LED+, LCM1602_IIC2.A
  N14: LCD2.LED-, LCM1602_IIC2.K
  GND: LCM1602_IIC2.GND, Bauteil1.GND, S1.Pin_1, S1.Pin_2, S2.Pin_3, S2.Pin_4, S3.Pin_3, S3.Pin_4, S4.Pin_3, S4.Pin_4, J1.pin1, VCC1.-, C1.2, R2.Pin_1, U1.G$1_V-
  VCC: LCM1602_IIC2.VCC, Bauteil1.5V, R3.Pin_0, U1.G$1_V+
  N15: LCM1602_IIC2.SDA, Bauteil1.A4
  N16: LCM1602_IIC2.SCL, Bauteil1.A5
  N17: LCM1602_IIC2.LED_A, LCM1602_IIC2.LED_B
  N18: Bauteil1.RESET, S1.Pin_3, S1.Pin_4
  N19: Bauteil1.D2, S2.Pin_1, S2.Pin_2
  N20: Bauteil1.D3, S3.Pin_1, S3.Pin_2
  N21: Bauteil1.D4, S4.Pin_1, S4.Pin_2
  N22: Bauteil1.D11/MOSI, J1.pin2, R1.Pin_1, U1.G$2_OUT
  N23: Bauteil1.VIN, VCC1.+
  N24: R1.Pin_0, C1.1, U1.G$2_+IN
  N25: R2.Pin_0, R3.Pin_1, U1.G$2_-IN

notes:
  R = 100 Ohm
  R2=R3 = 100K Ohm (beliebig)
  C1 = 4,7 nF Folie oder Keramik
  OPV als Komparator, Verstärkung unendlich

custom parts:
  LCM1602 IIC: I2C-Module to use a 1602 or 2004 LCD on with the wire.h libory Serial LCD Modul
